// Logisim project ALU74181.circ as structural Verilog: 1 circuit, main circuit 74181
module _74181 (
  input  [3:0] S,
  input  M,
  input  nCn,
  input  [3:0] A,
  input  [3:0] B,
  output [3:0] F,
  output nG,
  output nCn_4,
  output nP,
  output A_B
);

  wire and_1_out, and_2_out, and_3_out, and_4_out, and_5_out, and_6_out, and_7_out, and_8_out, and_9_out,
       and_10_out, and_11_out, and_12_out, and_13_out, and_14_out, and_15_out, and_16_out, and_17_out,
       and_18_out, and_19_out, and_20_out, and_21_out, and_22_out, and_23_out, and_24_out, and_26_out,
       and_27_out, and_28_out, and_29_out, and_30_out, and_31_out, and_32_out, and_33_out, and_34_out,
       and_35_out, and_36_out, and_37_out, and_38_out, nand_2_out, nand_4_out, nor_2_out, nor_3_out,
       nor_4_out, nor_5_out, nor_6_out, nor_7_out, nor_8_out, nor_9_out, nor_10_out, nor_11_out, nor_12_out,
       not_1_out, not_2_out, not_3_out, not_4_out, not_5_out, not_6_out, not_7_out, not_8_out, not_9_out;

  and and_1 (and_1_out, nor_3_out, nor_3_out);
  nor nor_1 (nG, and_1_out, and_3_out, and_2_out, and_4_out, and_4_out);
  and and_2 (and_2_out, nor_2_out, nor_4_out, nor_9_out);
  and and_3 (and_3_out, nor_2_out, nor_6_out);
  and and_4 (and_4_out, nor_2_out, nor_4_out, nor_8_out, nor_12_out, nor_12_out);
  nor nor_2 (nor_2_out, and_6_out, and_5_out);
  and and_5 (and_5_out, A[3], S[2], not_1_out);
  and and_6 (and_6_out, B[3], S[3], A[3]);
  not not_1 (not_1_out, B[3]);
  nand nand_1 (nCn_4, nG, nand_2_out);
  nand nand_2 (nand_2_out, nor_2_out, nor_4_out, nor_8_out, nor_11_out, nCn);
  nor nor_3 (nor_3_out, and_8_out, and_7_out, and_9_out);
  and and_7 (and_7_out, S[0], B[3]);
  and and_8 (and_8_out, not_1_out, S[1]);
  nand nand_3 (nP, nor_2_out, nor_4_out, nor_8_out, nor_11_out, nor_11_out);
  and and_9 (and_9_out, A[3], A[3]);
  and and_10 (and_10_out, nor_2_out, not_2_out);
  and and_11 (and_11_out, nor_4_out, nor_8_out, nor_11_out, nCn, not_9_out);
  not not_2 (not_2_out, nor_3_out);
  nor nor_4 (nor_4_out, and_12_out, and_13_out);
  and and_12 (and_12_out, B[2], S[3], A[2]);
  and and_13 (and_13_out, A[2], S[2], not_3_out);
  xor xor_1 (F[3], and_10_out, nor_5_out);
  nor nor_5 (nor_5_out, and_11_out, and_14_out, and_17_out, and_16_out, and_16_out);
  and and_14 (and_14_out, nor_4_out, nor_8_out, nor_12_out, not_9_out, not_9_out);
  and and_15 (and_15_out, not_3_out, S[1]);
  not not_3 (not_3_out, B[2]);
  and and_16 (and_16_out, nor_6_out, not_9_out);
  and and_17 (and_17_out, nor_4_out, nor_9_out, not_9_out);
  nor nor_6 (nor_6_out, and_15_out, and_18_out, and_19_out);
  and and_18 (and_18_out, S[0], B[2]);
  and and_19 (and_19_out, A[2], A[2]);
  and and_20 (and_20_out, nor_4_out, not_4_out);
  and and_21 (and_21_out, nor_8_out, nor_8_out, nor_11_out, nCn, not_9_out);
  not not_4 (not_4_out, nor_6_out);
  and and_22 (and_22_out, B[1], S[3], A[1]);
  xor xor_2 (F[2], and_20_out, nor_7_out);
  nor nor_7 (nor_7_out, and_21_out, and_23_out, and_27_out);
  and and_23 (and_23_out, nor_8_out, nor_12_out, not_9_out);
  nor nor_8 (nor_8_out, and_22_out, and_24_out);
  and and_24 (and_24_out, A[1], S[2], not_5_out);
  not not_5 (not_5_out, B[1]);
  and and_25 (A_B, F[3], F[3], F[2], F[1], F[0]);
  and and_26 (and_26_out, nor_8_out, not_6_out);
  and and_27 (and_27_out, nor_9_out, not_9_out);
  not not_6 (not_6_out, nor_9_out);
  nor nor_9 (nor_9_out, and_29_out, and_28_out, and_30_out);
  and and_28 (and_28_out, S[0], B[1]);
  and and_29 (and_29_out, not_5_out, S[1]);
  and and_30 (and_30_out, A[1], A[1]);
  xor xor_3 (F[1], and_26_out, nor_10_out);
  nor nor_10 (nor_10_out, and_32_out, and_31_out);
  and and_31 (and_31_out, nor_12_out, not_9_out);
  and and_32 (and_32_out, nCn, nor_11_out, not_9_out);
  nor nor_11 (nor_11_out, and_33_out, and_34_out);
  and and_33 (and_33_out, B[0], S[3], A[0]);
  and and_34 (and_34_out, A[0], S[2], not_7_out);
  not not_7 (not_7_out, B[0]);
  and and_35 (and_35_out, nor_11_out, not_8_out);
  not not_8 (not_8_out, nor_12_out);
  nor nor_12 (nor_12_out, and_37_out, and_36_out, and_38_out);
  and and_36 (and_36_out, S[0], B[0]);
  and and_37 (and_37_out, not_7_out, S[1]);
  xor xor_4 (F[0], and_35_out, nand_4_out);
  and and_38 (and_38_out, A[0], A[0]);
  not not_9 (not_9_out, M);
  nand nand_4 (nand_4_out, not_9_out, nCn);
endmodule
