// Logisim project CustomALU.circ as structural Verilog: 1 circuit, main circuit main
module main (
  input  [3:0] A,
  input  [3:0] B,
  input  [3:0] INST,
  output Cout,
  output [3:0] S
);

  wire nand_1_out, nand_2_out, nand_3_out, nand_4_out, nor_1_out, nor_2_out, nor_3_out, nor_4_out;
  wire [3:0] adder_1_out, multiplexer_1_out, multiplexer_2_out, multiplexer_3_out, xor_4_out, xor_8_out,
       xor_12_out, xor_16_out, xor_20_out;

  xor xor_1 (xor_4_out[3], B[3], INST[0]);
  xor xor_2 (xor_4_out[2], B[2], INST[0]);
  xor xor_3 (xor_4_out[1], B[1], INST[0]);
  xor xor_4 (xor_4_out[0], B[0], INST[0]);
  xor xor_5 (xor_8_out[3], B[3], A[3]);
  xor xor_6 (xor_8_out[2], B[2], A[2]);
  xor xor_7 (xor_8_out[1], B[1], A[1]);
  xor xor_8 (xor_8_out[0], B[0], A[0]);
  nand nand_1 (nand_1_out, B[3], A[3]);
  nand nand_2 (nand_2_out, B[2], A[2]);
  nand nand_3 (nand_3_out, B[1], A[1]);
  nand nand_4 (nand_4_out, B[0], A[0]);
  nor nor_1 (nor_1_out, B[3], A[3]);
  nor nor_2 (nor_2_out, B[2], A[2]);
  nor nor_3 (nor_3_out, B[1], A[1]);
  nor nor_4 (nor_4_out, B[0], A[0]);
  xor xor_9 (xor_12_out[3], B[3], INST[0]);
  xor xor_10 (xor_12_out[2], B[2], INST[0]);
  xor xor_11 (xor_12_out[1], B[1], INST[0]);
  xor xor_12 (xor_12_out[0], B[0], INST[0]);
  Adder #(.width(4)) adder_1 (.a(A), .b(xor_4_out), .out(adder_1_out), .cin(INST[0]), .cout(Cout));
  xor xor_13 (xor_16_out[3], INST[0], nand_1_out);
  xor xor_14 (xor_16_out[2], INST[0], nand_2_out);
  xor xor_15 (xor_16_out[1], INST[0], nand_3_out);
  xor xor_16 (xor_16_out[0], INST[0], nand_4_out);
  xor xor_17 (xor_20_out[3], INST[0], nor_1_out);
  xor xor_18 (xor_20_out[2], INST[0], nor_2_out);
  xor xor_19 (xor_20_out[1], INST[0], nor_3_out);
  xor xor_20 (xor_20_out[0], INST[0], nor_4_out);
  Multiplexer #(.width(4), .enable("false")) multiplexer_1 (
    .in0(xor_16_out), .in1(xor_20_out), .out(multiplexer_1_out), .sel(INST[1]));
  Multiplexer #(.width(4), .enable("false")) multiplexer_2 (
    .in0(xor_8_out), .in1(adder_1_out), .out(multiplexer_2_out), .sel(INST[2]));
  Multiplexer #(.width(4), .enable("false")) multiplexer_3 (
    .in0(xor_12_out), .in1(multiplexer_1_out), .out(multiplexer_3_out), .sel(INST[2]));
  Multiplexer #(.width(4), .enable("false")) multiplexer_4 (
    .in0(multiplexer_3_out), .in1(multiplexer_2_out), .out(S), .sel(INST[3]));
  // NOT_Gate not_1 is placed but not wired
endmodule
