// Logisim project IR_decoder.circ as structural Verilog: 1 circuit, main circuit main
module main (
  input  in_1,
  input  Clk,
  input  CLR,
  input  [3:0] Instruction,
  output IR_en,
  output D_en,
  output OUT_en,
  output A_en,
  output Car_en,
  output Car_mux,
  output MUX,
  output [3:0] S,
  output M,
  output nCn
);

  wire decoder_1_out0, decoder_1_out1, decoder_1_out2, decoder_1_out3, decoder_1_out4, decoder_1_out5,
       decoder_1_out6, decoder_1_out7, decoder_1_out8, decoder_1_out9, decoder_1_out10, decoder_1_out11,
       decoder_1_out12, decoder_2_out1, decoder_2_out2, nor_1_out, or_7_out, or_8_out;
  wire [1:0] counter_1_q;

  Decoder #(.select(4), .disabled(0), .enable("false")) decoder_1 (
    .out0(decoder_1_out0), .out1(decoder_1_out1), .out2(decoder_1_out2), .out3(decoder_1_out3),
    .out4(decoder_1_out4), .out5(decoder_1_out5), .out6(decoder_1_out6), .out7(decoder_1_out7),
    .out8(decoder_1_out8), .out9(decoder_1_out9), .out10(decoder_1_out10), .out11(decoder_1_out11),
    .out12(decoder_1_out12), .sel(Instruction));  // open: out13, out14, out15
  Counter #(.width(2), .max('h2)) counter_1 (
    .count(in_1), .Q(counter_1_q), .clk(Clk), .clr(CLR));  // open: load, D, carry
  Decoder #(.select(2), .disabled(0), .enable("false")) decoder_2 (
    .out0(IR_en), .out1(decoder_2_out1), .out2(decoder_2_out2), .sel(counter_1_q));  // open: out3
  and and_1 (D_en, decoder_2_out1, nor_1_out);
  nor nor_1 (nor_1_out, decoder_1_out0, decoder_1_out2, decoder_1_out9, decoder_1_out10);
  or or_1 (S[3], decoder_1_out1, decoder_1_out2, decoder_1_out3, decoder_1_out4, decoder_1_out10);
  or or_2 (S[2], decoder_1_out2, decoder_1_out5, decoder_1_out6, decoder_1_out10, decoder_1_out11, decoder_1_out12);
  or or_3 (S[1], decoder_1_out1, decoder_1_out2, decoder_1_out5, decoder_1_out6, decoder_1_out10, decoder_1_out11, decoder_1_out12);
  or or_4 (S[0], decoder_1_out2, decoder_1_out3, decoder_1_out4, decoder_1_out7, decoder_1_out8, decoder_1_out10);
  or or_5 (M, decoder_1_out1, decoder_1_out2, decoder_1_out7, decoder_1_out8);
  or or_6 (nCn, decoder_1_out3, decoder_1_out4, decoder_1_out10, decoder_1_out5, decoder_1_out6);
  and and_2 (OUT_en, decoder_2_out2, or_7_out);
  or or_7 (or_7_out, decoder_1_out2, decoder_1_out4, decoder_1_out6, decoder_1_out8, decoder_1_out12);
  and and_3 (A_en, decoder_2_out2, ~decoder_1_out0, ~decoder_1_out2);  // AND_Gate
  or or_8 (or_8_out, decoder_1_out5, decoder_1_out6);
  and and_4 (MUX, decoder_2_out2, or_8_out);
  and and_5 (Car_en, decoder_2_out2, ~M);  // AND_Gate
  or or_9 (Car_mux, decoder_1_out12, decoder_1_out11, decoder_1_out10);

  // Notes on the sheet:
  //   Sequencer. Fetch. Decode. Execute
  //   S3
  //   S2
  //   S1
  //   S0
  //   M
  //   /Cn
endmodule
