// Logisim project MicroProcessor.circ as structural Verilog: 1 circuit, main circuit main
module main (
  input  [3:0] Data,
  input  [3:0] Instruction,
  input  _0,
  input  Clock,
  input  CLR,
  input  ENABLE,
  input  [3:0] in_7,
  input  [3:0] in_8,
  input  in_9,
  input  in_10,
  input  [3:0] in_11,
  output [3:0] OUTPUT,
  output [1:0] Z_C,
  output [3:0] out_14,
  output out_15,
  output out_16,
  output out_17,
  output out_18
);

  wire main_1_a_en, main_1_car_en, main_1_car_mux, main_1_d_en, main_1_ir_en, main_1_m, main_1_mux,
       main_1_ncn, main_1_out_en, multiplexer_2_out, nor_1_out, not_1_out;
  wire [1:0] n74181_1_a_b;
  wire [3:0] main_1_s, multiplexer_1_out, n74181_1_f, register_1_q, register_2_q, register_3_q;

  Register #(.width(4)) register_1 (.D(Data), .en(main_1_d_en), .Q(register_1_q), .clk(Clock), .clr(CLR));
  Register #(.width(4)) register_2 (.D(Instruction), .en(main_1_ir_en), .Q(register_2_q), .clk(Clock), .clr(CLR));
  IR_decoder_main main_1 (
    .in_1(ENABLE), .Clk(Clock), .Instruction(register_2_q), .MUX(main_1_mux), .IR_en(main_1_ir_en),
    .D_en(main_1_d_en), .OUT_en(main_1_out_en), .A_en(main_1_a_en), .M(main_1_m), .nCn(main_1_ncn),
    .S(main_1_s), .CLR(CLR), .Car_en(main_1_car_en), .Car_mux(main_1_car_mux));
  Register #(.width(4)) register_3 (.D(multiplexer_1_out), .en(main_1_a_en), .Q(register_3_q), .clk(Clock), .clr(CLR));
  _74181 u_74181_1 (
    .M(main_1_m), .nCn(main_1_ncn), .nCn_4(n74181_1_a_b[1]), .A_B(n74181_1_a_b[0]), .S(main_1_s),
    .A(register_3_q), .B(register_1_q), .F(n74181_1_f));  // open: nG, nP
  Multiplexer #(.width(4), .disabled(0), .enable("false")) multiplexer_1 (
    .in0(n74181_1_f), .in1({{2{_0}}, n74181_1_a_b}), .out(multiplexer_1_out), .sel(main_1_mux));
  not not_1 (not_1_out, n74181_1_a_b[1]);
  Multiplexer #(.disabled(0), .enable("false")) multiplexer_2 (
    .in0(not_1_out), .in1(n74181_1_a_b[1]), .out(multiplexer_2_out), .sel(main_1_car_mux));
  _74181 u_74181_2 (
    .M(in_9), .nCn(in_10), .nG(out_18), .nCn_4(out_16), .nP(out_17), .A_B(out_15), .S(in_11), .A(in_7),
    .B(in_8), .F(out_14));
  nor nor_1 (nor_1_out, multiplexer_1_out[3], multiplexer_1_out[2], multiplexer_1_out[1], multiplexer_1_out[0]);
  Register #(.width(4)) register_4 (.D(multiplexer_1_out), .en(main_1_out_en), .Q(OUTPUT), .clk(Clock), .clr(CLR));
  D_Flip_Flop d_ff_1 (.clk(Clock), .D(nor_1_out), .Q(Z_C[1]), .en(main_1_a_en), .reset(CLR));  // open: Qn, preset
  D_Flip_Flop d_ff_2 (
    .clk(Clock), .D(multiplexer_2_out), .Q(Z_C[0]), .en(main_1_car_en), .reset(CLR));  // open: Qn, preset
endmodule
