// Logisim project Microprocessor_v2.circ as structural Verilog: 1 circuit, main circuit main
module main (
  input  [3:0] Data,
  input  [3:0] Instruction,
  input  Clock
);

  wire buffer_1_out, d_ff_1_q, main_1_cout, not_1_out;
  wire [3:0] buffer_2_out, main_1_s, register_1_q, register_2_q, register_3_q;

  Register #(.width(4)) register_1 (.D(Data), .en(1'b1), .Q(register_1_q), .clk(Clock));  // open: clr
  Register #(.width(4)) register_2 (.D(Instruction), .en(1'b1), .Q(register_2_q), .clk(Clock));  // open: clr
  not not_1 (not_1_out, Clock);
  CustomALU_main main_1 (.A(register_3_q), .B(register_1_q), .INST(register_2_q), .Cout(main_1_cout), .S(main_1_s));
  D_Flip_Flop d_ff_1 (.clk(not_1_out), .D(main_1_cout), .Q(d_ff_1_q), .en(1'b1));  // open: Qn, preset, reset
  Register #(.width(4)) register_3 (.D(main_1_s), .en(1'b1), .Q(register_3_q), .clk(not_1_out));  // open: clr
  buf buffer_1 (buffer_1_out, d_ff_1_q);
  assign buffer_2_out = register_3_q;  // Buffer buffer_2, 4 bits wide
  LED led_1 (.in(buffer_2_out[3]));
  LED led_2 (.in(buffer_1_out));
  LED led_3 (.in(buffer_2_out[1]));
  LED led_4 (.in(buffer_2_out[0]));
  LED led_5 (.in(buffer_2_out[2]));
endmodule
